# Fritzing sketch routeursolaire (saved by Fritzing 1.0.3b)

parts:
  M1 = ac light dimmer 3terminal
  M2 = ac light dimmer 3terminal
  M3 = ac light dimmer 3terminal
  U1 = ESP32-38PinWide [part_number=ESP32-38PinWide]
  Chauffe_eau = bulb
  M4 = JSY-MK-194T
  Pince_Amperemetrique = JSY-MK-194T sensor2
  Chauffages_1 = bulb
  Chauffages_2 = bulb
  220V_sortie_tableau_éléctique = 2.1mm Barrel Jack with Terminal Block
  5V_to_3_3V = AMS1777 5V regulator module
  ZS-042_RTC1 = ZS-042 RTC Module
  220V_EDF = 2.1mm Barrel Jack with Terminal Block
  220V_Entree_Tableau = 2.1mm Barrel Jack with Terminal Block
  S1 = Taiway 100-SP-X-T1 SPDT Miniature Toggle Switch [part_number=100-SP-X-T1-0-0-B1-M1 package=THT]
  OLED_I2C2 = OLED 128x64 I2C Monochrome Display V2

nets:
  VCC: M1.VCC, M2.VCC, M3.VCC, M4.VCC, 5V_to_3_3V.VOUT+, ZS-042_RTC1.VCC, OLED_I2C2.VCC
  GND: M1.GND, M2.GND, M3.GND, U1.GND, M4.GND, 5V_to_3_3V.GND-_(input), ZS-042_RTC1.GND, OLED_I2C2.GND
  N1: M1.PWM, M2.PWM, U1.GPIO26
  N2: M1.OUT, Chauffages_1.2
  N3: M1.N, M2.N, M3.N, Chauffe_eau.1, M4.UN, Chauffages_1.1, Chauffages_2.1, 220V_sortie_tableau_éléctique.POS
  N4: M1.IN, M2.IN, M3.IN, M4.UL, 220V_sortie_tableau_éléctique.NEG
  N5: M2.OUT, Chauffages_2.2
  N6: M3.Z-C, U1.GPIO35
  N7: M3.PWM, U1.GPIO25
  N8: M3.OUT, Chauffe_eau.2
  N9: U1.3.3, S1.COM
  N10: U1.GPIO34, S1.L2
  N11: U1.VIN, 5V_to_3_3V.VIN+
  N12: U1.GPIO16, M4.TX
  N13: U1.GPIO17, M4.PF, M4.RX
  N14: U1.GPIO21, ZS-042_RTC1.SDA, OLED_I2C2.SDA
  N15: U1.GPIO22, U1.GPIO23, ZS-042_RTC1.SCL, OLED_I2C2.SCL
  N16: M4.JP1-a, Pince_Amperemetrique.Black
  N17: M4.JP1-b, Pince_Amperemetrique.Red
  N18: 220V_EDF.POS, 220V_Entree_Tableau.POS
  N19: 220V_EDF.NEG, 220V_Entree_Tableau.NEG

custom parts:
  ac light dimmer 3terminal: ac light dimmer module 3 output terminals.
  ESP32-38PinWide: Generic 38-Pin ESP32 with wide format (only access to one side of pins on a breadboard) based on Stephen Lilley's HiLetgo ESP-WROOM-32 ESP32 ESP-32S Development Board.
  JSY-MK-194T: AC Single Phase Bidirectional Power Energy Meter Module
  JSY-MK-194T sensor2: Sensor 2 for JSY-MK-194T
  AMS1777 5V regulator module: AMS1777 5V regulator module source : https://github.com/ShenTengTu/fritzing_parts/tree/master/voltage%20regulator/AMS1117_5V_regulator_module
  OLED 128x64 I2C Monochrome Display V2: OLED 128x64 I2C Monochrome Display
